// Logisim project datapath.circ as structural Verilog: 4 circuits, main circuit main
module main (
  output [15:0] out_1,
  output [3:0] out_2
);

  wire ALUHi, ALULo, chkZ, CLK, DrALU, DrMEM, DrOFF, DrPC, DrREG, LdA, LdB, LdIR, LdMAR, LdPC, LdZ, OpTest,
       RegSelHi, RegSelLo, WrMEM, WrREG, Z;
  wire [2:0] OP;
  wire [3:0] datapath_1_ry, datapath_1_rz, multiplexer_1_out;

  Clock clock_1 (.out(CLK));
  Datapath datapath_1 (
    .out_17(out_1), .func({ALUHi, ALULo}), .LdA(LdA), .LdMAR(LdMAR), .DrPC(DrPC), .DrReg(DrREG),
    .DrOff(DrOFF), .WrReg(WrREG), .LdPC(LdPC), .LdB(LdB), .LdIR(LdIR), .DrALU(DrALU), .DrMEM(DrMEM),
    .WrMem(WrMEM), .RegNo(multiplexer_1_out), .CLK(CLK), .LdZ(LdZ), .OP(OP), .RX(out_2), .RY(datapath_1_ry),
    .RZ(datapath_1_rz), .Z(Z));
  Multiplexer #(.select(2), .width(4)) multiplexer_1 (
    .in0(out_2), .in1(datapath_1_ry), .in2(datapath_1_rz), .out(multiplexer_1_out), .sel({RegSelHi, RegSelLo}));  // open: in3, en
  Microcontroller microcontroller_1 (
    .OP(OP), .CLK(CLK), .Z(Z), .DrReg(DrREG), .LdPC(LdPC), .WrReg(WrREG), .DrMem(DrMEM), .LdIR(LdIR),
    .WrMem(WrMEM), .DrALU(DrALU), .LdMAR(LdMAR), .RegSelLo(RegSelLo), .DrPc(DrPC), .LdA(LdA),
    .RegSelHi(RegSelHi), .DrOff(DrOFF), .LdB(LdB), .ALULo(ALULo), .ALUHi(ALUHi), .LdZ(LdZ), .OPTest(OpTest),
    .chkZ(chkZ));
endmodule

// opcode
module ALU (
  input  [15:0] A,
  input  [15:0] B,
  input  [1:0] in_3,
  output [15:0] ALUOut
);

  wire undriven;
  wire [15:0] adder_1_out, adder_2_out, nand_1_out, subtractor_1_out;

  Adder #(.width(16)) adder_1 (.a(A), .b(B), .out(adder_1_out));  // open: cin, cout
  Adder #(.width(16)) adder_2 (.a(A), .b(16'h1), .out(adder_2_out));  // open: cin, cout
  Subtractor #(.width(16)) subtractor_1 (.a(A), .b(B), .out(subtractor_1_out));  // open: bin, bout
  assign nand_1_out = ~(A & B);  // NAND_Gate nand_1, 16 bits wide
  Multiplexer #(.select(2), .width(16)) multiplexer_1 (
    .in0(adder_1_out), .in1(nand_1_out), .in2(subtractor_1_out), .in3(adder_2_out), .out(ALUOut), .sel(in_3),
    .en(undriven));
endmodule

module Microcontroller (
  input  [2:0] OP,
  input  CLK,
  input  Z,
  output DrReg,
  output LdPC,
  output WrReg,
  output DrMem,
  output LdIR,
  output WrMem,
  output DrALU,
  output LdMAR,
  output RegSelLo,
  output DrPc,
  output LdA,
  output RegSelHi,
  output DrOff,
  output LdB,
  output ALULo,
  output ALUHi,
  output LdZ,
  output OPTest,
  output chkZ
);

  wire button_1_out;
  wire [5:0] multiplexer_1_out, nextState, rom_2_data, rom_3_data, State, undriven;

  ROM #(.addrWidth(6), .dataWidth(25)) rom_1 (
    .addr(State),
    .data({chkZ, OPTest, ALUHi, ALULo, RegSelHi, RegSelLo, WrMem, WrReg, LdZ, LdB, LdA, LdMAR, LdIR, LdPC, DrOff, DrPc, DrALU, DrMem, DrReg, nextState}));  // open: sel
  ROM #(.addrWidth(3), .dataWidth(6)) rom_2 (.addr(OP), .data(rom_2_data));  // open: sel
  ROM #(.addrWidth(2), .dataWidth(6)) rom_3 (.addr({1'b0, Z}), .data(rom_3_data));  // open: sel
  Multiplexer #(.select(2), .width(6)) multiplexer_1 (
    .in0(nextState), .in1(rom_2_data), .in2(rom_3_data), .in3(undriven), .out(multiplexer_1_out),
    .sel({chkZ, OPTest}));  // open: en
  Register #(.width(6)) register_1 (.D(multiplexer_1_out), .Q(State), .clk(CLK));  // open: en, clr
  Clock clock_1 ();  // open: out
  Button button_1 (.out(button_1_out));

  // Notes on the sheet:
  //   contents of rom_1 (hex, n*v repeats v):
  //   6201 1082 e00900 4044 88045 1410100 6202 4208 8409 900 a020b 840 8404d 10804e 20100 84050 8411 20100
  //   84053 8414 2115 20080 84057 108058 220100 8405a 841b 211c 40040 1d
  //   contents of rom_2 (hex, n*v repeats v):
  //   c 16 f 12 19 3 a 1d
  //   contents of rom_3 (hex, n*v repeats v):
  //   6 7
endmodule

module Datapath (
  input  [1:0] func,
  input  LdA,
  input  LdMAR,
  input  DrPC,
  input  DrReg,
  input  DrOff,
  input  WrReg,
  input  LdPC,
  input  LdB,
  input  LdIR,
  input  DrALU,
  input  DrMEM,
  input  WrMem,
  input  [3:0] RegNo,
  input  CLK,
  input  LdZ,
  output [15:0] out_17,
  output [2:0] OP,
  output [3:0] RX,
  output [3:0] RY,
  output [3:0] RZ,
  output Z
);

  wire comparator_1_eq, comparator_2_eq, not_1_out;
  wire [4:4] IR_q;
  wire [15:0] A_q, alu_1_aluout, B_q, bit_extender_1_out, DrReg_out, MAR_q, multiplexer_1_out, PC_q,
       ram_1_data;

  Register #(.width(16)) PC (.D(DrReg_out), .en(LdPC), .Q(PC_q), .clk(CLK));  // open: clr
  Register #(.width(16)) A (.D(DrReg_out), .en(LdA), .Q(A_q), .clk(CLK));  // open: clr
  assign DrReg_out = DrPC ? PC_q : 16'bz;  // Controlled_Buffer DrReg
  Register #(.width(16)) B (.D(DrReg_out), .en(LdB), .Q(B_q), .clk(CLK));  // open: clr
  ALU alu_1 (.A(B_q), .B(A_q), .in_3(func), .ALUOut(alu_1_aluout));
  assign DrReg_out = DrALU ? alu_1_aluout : 16'bz;  // Controlled_Buffer DrALU
  Register #(.width(16)) MAR (.D(DrReg_out), .en(LdMAR), .Q(MAR_q), .clk(CLK));  // open: clr
  RAM #(.addrWidth(4), .dataWidth(16), .bus("separate")) ram_1 (
    .addr(RegNo), .din(DrReg_out), .data(ram_1_data), .str(WrReg), .clk(CLK));  // open: sel, ld, clr
  RAM #(.addrWidth(16), .dataWidth(16), .bus("separate")) ram_2 (
    .addr(MAR_q), .din(DrReg_out), .data(out_17), .str(WrMem), .clk(CLK));  // open: sel, ld, clr
  assign DrReg_out = DrMEM ? out_17 : 16'bz;  // Controlled_Buffer DrMem
  Register #(.width(16)) IR (.D(DrReg_out), .en(LdIR), .Q({OP, RX, RY, IR_q[4], RZ}), .clk(CLK));  // open: clr
  Comparator #(.width(4)) comparator_1 (.a(RegNo), .b(4'b0000), .eq(comparator_1_eq));  // open: gt, lt
  not not_1 (not_1_out, comparator_1_eq);
  Multiplexer #(.width(16)) multiplexer_1 (
    .in0({16{1'b0}}), .in1(ram_1_data), .out(multiplexer_1_out), .sel(not_1_out));  // open: en
  assign DrReg_out = DrReg ? multiplexer_1_out : 16'bz;  // Controlled_Buffer DrReg_2
  Register #(.width(1)) register_1 (.D(comparator_2_eq), .en(LdZ), .Q(Z), .clk(CLK));  // open: clr
  assign bit_extender_1_out = {{11{1'b0}}, {IR_q[4], RZ}};  // Bit_Extender bit_extender_1
  Comparator #(.width(16)) comparator_2 (.a(DrReg_out), .b({16{1'b0}}), .eq(comparator_2_eq));  // open: gt, lt
  assign DrReg_out = DrOff ? bit_extender_1_out : 16'bz;  // Controlled_Buffer DrOff

  // Other names for the same wires on the sheet: outMem[15:0] = out_17
endmodule
